# Fritzing sketch GreenhouseDifferential (saved by Fritzing 0.9.3b)
breadboards: 2

parts:
  Part1 = Arduino Uno (Rev3)
  R1 = Resistor [tolerance=±5% resistance=220 package=THT]
  R2 = Resistor [tolerance=±5% resistance=220 package=THT]
  R3 = Resistor [tolerance=±5% resistance=220 package=THT]
  R4 = Resistor [tolerance=±5% resistance=220 package=THT]
  R5 = Resistor [tolerance=±5% resistance=220 package=THT]
  LED1 = LED - 5mm [color="Red (633nm)" package="5 mm [THT]"]
  LED2 = LED - 5mm [color="Yellow (595nm)" package="5 mm [THT]"]
  LED3 = LED - 5mm [color="Green (555nm)" package="5 mm [THT]"]
  LED4 = LED - 5mm [color="Blue (470nm)" package="5 mm [THT]"]
  LED5 = LED - 5mm [color="White (6500K)" package="5 mm [THT]"]
  Part2 = Arduino Mega 2560 (Rev3)
  R6 = Resistor [tolerance=±5% resistance=220 package=THT]
  R7 = Resistor [tolerance=±5% resistance=220 package=THT]
  R8 = Resistor [tolerance=±5% resistance=220 package=THT]
  LED6 = RGB LED (com. cathode, rgb) [package="5 mm [THT]"]
  R9 = Photocell (LDR) [package=THT]
  J1 = Piezo Speaker
  U1 = LM 358 Dual Op-Amp [package="DIP8 [THT]"]
  R10 = Resistor [tolerance=±5% resistance=220 package=THT]
  R11 = Resistor [tolerance=±5% resistance=220 package=THT]
  R12 = Resistor [tolerance=±5% resistance=220 package=THT]
  R13 = Resistor [tolerance=±5% resistance=220 package=THT]

nets:
  N1: Part1.D0/RX, R5.Pin_1
  N2: Part1.D2, R4.Pin_1
  N3: Part1.D3_PWM, R3.Pin_1
  N4: Part1.D4, R2.Pin_1
  N5: Part1.D5_PWM, R1.Pin_1
  N6: Part1.GND, LED1.cathode, LED2.cathode, LED3.cathode, LED4.cathode, LED5.cathode
  N7: R1.Pin_0, LED1.anode
  N8: R2.Pin_0, LED2.anode
  N9: R3.Pin_0, LED3.anode
  N10: R4.Pin_0, LED4.anode
  N11: R5.Pin_0, LED5.anode
  N12: Part2.A0, Part2.GND, LED6.green_anode, J1.pin1, R11.Pin_0, R13.Pin_0
  N13: Part2.D9_PWM, J1.pin2
  N14: Part2.5V, R10.Pin_0
  N15: Part2.D2_PWM, R7.Pin_1
  N16: Part2.D4_PWM, R6.Pin_1
  N17: Part2.D6_PWM, R8.Pin_1
  N18: R6.Pin_0, LED6.common_cathode
  N19: R7.Pin_0, LED6.blue_anode
  N20: R8.Pin_0, LED6.red_anode
  N21: R9.pin_0, U1.connector2, R10.Pin_1, R11.Pin_1
  N22: U1.connector0, R12.Pin_0
  N23: U1.connector1, R12.Pin_1, R13.Pin_1
